# Fritzing sketch Untitled Sketch (saved by Fritzing 1.0.7)
stripboards: 1

parts:
  WeMos_D1_Mini1 = WeMos D1 Mini  # not connected
  Bauteil1 = ADS1015  # not connected
  XL1 = XL6009 Step-Up module
  Bauteil2 = XY-ItoV [part_number=XY-ITOV]
  J1 = Camdenboss CTB0158-2 [part_number=CTB0158-2 package=THT]
  J2 = Camdenboss CTB0158-2 [part_number=CTB0158-2 package=THT]

nets:
  N1: XL1.IN+, XL1.OUT+, Bauteil2.VCC, J1.pin2, J2.pin2
  N2: XL1.IN-, XL1.OUT-, Bauteil2.GND, Bauteil2.VOUT, J1.pin1
  N3: Bauteil2.I+, J2.pin1

notes:
  Sensor -
  Sensor +
  5V +
  24 V +
  GND
  VOUT
  5V -
  3,3V +

custom parts:
  ADS1015: ADC ADS1015
  XL6009 Step-Up module: XL6009 DC-DC Step UP Power Supply Module --> 5V~35V, 4A.
  XY-ItoV: Current to voltage converter In the process of circuit signal transmission, the voltage signal will weaken with the increase of the transmission distance, and the current transmission can avoid the weakening of the signal. The module is used for the end of current signal transmission, the signal is converted into voltage signal for SCM detection. The current input supports 4-20 mA and 0-20 mA,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
